// Logisim project 6.circ as structural Verilog: 1 circuit, main circuit main
module main (
);

  wire a, and_1_out, and_2_out, and_3_out, and_4_out, and_5_out, and_6_out, and_7_out, and_8_out, and_9_out,
       and_10_out, and_11_out, and_12_out, and_13_out, and_14_out, and_15_out, and_16_out, and_17_out, b, c,
       clock_1_out, d, e, f, g, not_1_out, not_2_out, not_3_out, not_4_out, not_5_out, Reset_out, stop, w0,
       w1, w2, w3;

  not not_1 (not_1_out, w0);
  not not_2 (not_2_out, w1);
  not not_3 (not_3_out, w2);
  not not_4 (not_4_out, w3);
  and and_1 (and_1_out, not_1_out, not_3_out);
  and and_2 (and_2_out, w2, w0);
  and and_3 (and_3_out, w1, w0);
  and and_4 (and_4_out, not_2_out, not_1_out);
  and and_5 (and_5_out, not_3_out, not_1_out);
  and and_6 (and_6_out, w1, not_1_out);
  and and_7 (and_7_out, not_3_out, w1);
  and and_8 (and_8_out, w2, not_2_out, w0);
  and and_9 (and_9_out, not_3_out, not_1_out);
  and and_10 (and_10_out, w1, not_1_out);
  and and_11 (and_11_out, not_2_out, not_1_out);
  and and_12 (and_12_out, w2, not_2_out);
  and and_13 (and_13_out, w2, not_1_out);
  and and_14 (and_14_out, not_3_out, w1);
  and and_15 (and_15_out, w1, not_1_out);
  and and_16 (and_16_out, w2, not_2_out);
  or or_1 (a, w1, w3, and_1_out, and_2_out);
  or or_2 (b, not_3_out, and_3_out, and_4_out);
  or or_3 (c, w0, not_2_out, w2);
  or or_4 (d, w3, and_5_out, and_6_out, and_7_out, and_8_out);
  or or_5 (f, and_11_out, w3, and_12_out, and_13_out);
  or or_6 (g, and_14_out, w3, and_15_out, and_16_out);
  or or_7 (e, and_9_out, and_10_out);
  _7_Segment_Display u_7_segment_display_1 (.g(g), .f(f), .a(a), .b(b), .e(e), .d(d), .c(c));  // open: dp
  Clock clock_1 (.out(clock_1_out));
  // Probe on {w3, w2, w1, w0}
  and and_17 (and_17_out, clock_1_out, not_5_out);
  not not_5 (not_5_out, stop);
  TTY #(.rows(10), .cols(1)) tty_1 (.data({3'b100, d, c, b, a}), .clk(and_17_out), .clr(Reset_out));  // open: we
  Counter #(.width(4), .max('h9), .ongoal("stay")) counter_1 (
    .Q({w3, w2, w1, w0}), .carry(stop), .clk(and_17_out), .clr(Reset_out));  // open: load, D, count
  TTY #(.rows(10), .cols(1)) tty_2 (.data({4'b0110, g, f, e}), .clk(and_17_out), .clr(Reset_out));  // open: we
  Button Reset (.out(Reset_out));

  // Notes on the sheet:
  //   O
  //   F
  //   K
  //   O
  //   F
  //   M
  //   M
  //   G
  //   O
  //   3
  //   0
  //   5
  //   4
  //   6
  //   6
  //   7
  //   0
  //   7
endmodule
