// Logisim project 4.circ as structural Verilog: 1 circuit, main circuit main
module main (
);

  wire and_1_out, and_2_out, and_3_out, Carry, CLK, clock_1_out, counter_1_carry, D0, D1, D2, D3, Enable,
       Load, multiplexer_1_out, multiplexer_2_out, multiplexer_3_out, multiplexer_4_out, nand_1_out,
       nand_2_out, nand_3_out, nand_4_out, nand_5_out, nand_6_out, nand_7_out, nand_8_out, nand_9_out,
       nand_10_out, nand_11_out, nand_12_out, nand_13_out, nand_14_out, nand_15_out, nand_16_out,
       nand_17_out, nand_18_out, nand_19_out, nand_20_out, nand_21_out, nand_22_out, nand_23_out,
       nand_24_out, nand_25_out, nand_26_out, nand_27_out, nand_28_out, nand_29_out, nand_30_out,
       nand_31_out, nand_32_out, not_1_out, Q0, Q1, Q2, Q3;
  wire [5:1] counter_1_q;

  and and_1 (and_1_out, Enable, Q0);
  and and_2 (and_2_out, and_1_out, Q1);
  and and_3 (and_3_out, and_2_out, Q2);
  and and_4 (Carry, and_3_out, Q3);
  nand nand_1 (nand_1_out, Q0, Enable);
  nand nand_2 (nand_2_out, Q1, and_1_out);
  nand nand_3 (nand_3_out, Q2, and_2_out);
  nand nand_4 (nand_4_out, Q3, and_3_out);
  nand nand_5 (nand_5_out, Q0, nand_1_out);
  nand nand_6 (nand_6_out, nand_1_out, Enable);
  nand nand_7 (nand_7_out, Q1, nand_2_out);
  nand nand_8 (nand_8_out, nand_2_out, and_1_out);
  nand nand_9 (nand_9_out, Q2, nand_3_out, nand_3_out);
  nand nand_10 (nand_10_out, nand_3_out, nand_3_out, and_2_out);
  nand nand_11 (nand_11_out, Q3, nand_4_out, nand_4_out);
  nand nand_12 (nand_12_out, nand_4_out, nand_4_out, and_3_out);
  nand nand_13 (nand_13_out, nand_5_out, nand_6_out);
  nand nand_14 (nand_14_out, nand_7_out, nand_8_out);
  nand nand_15 (nand_15_out, nand_9_out, nand_10_out);
  nand nand_16 (nand_16_out, nand_11_out, nand_12_out);
  Multiplexer multiplexer_1 (.in0(nand_13_out), .in1(D0), .out(multiplexer_1_out), .sel(Load));  // open: en
  Multiplexer multiplexer_2 (.in0(nand_14_out), .in1(D1), .out(multiplexer_2_out), .sel(Load));  // open: en
  Multiplexer multiplexer_3 (.in0(nand_15_out), .in1(D2), .out(multiplexer_3_out), .sel(Load));  // open: en
  Multiplexer multiplexer_4 (.in0(nand_16_out), .in1(D3), .out(multiplexer_4_out), .sel(Load));  // open: en
  nand nand_17 (nand_17_out, Q0, multiplexer_1_out);
  nand nand_18 (nand_18_out, Q1, multiplexer_2_out);
  nand nand_19 (nand_19_out, Q2, multiplexer_3_out);
  nand nand_20 (nand_20_out, Q3, multiplexer_4_out);
  nand nand_21 (nand_21_out, Q0, nand_17_out);
  nand nand_22 (nand_22_out, nand_17_out, multiplexer_1_out);
  nand nand_23 (nand_23_out, Q1, nand_18_out);
  nand nand_24 (nand_24_out, nand_18_out, multiplexer_2_out);
  nand nand_25 (nand_25_out, nand_21_out, nand_22_out);
  nand nand_26 (nand_26_out, Q2, nand_19_out);
  nand nand_27 (nand_27_out, nand_19_out, multiplexer_3_out);
  nand nand_28 (nand_28_out, Q3, nand_20_out);
  nand nand_29 (nand_29_out, nand_20_out, multiplexer_4_out);
  nand nand_30 (nand_30_out, nand_23_out, nand_24_out);
  nand nand_31 (nand_31_out, nand_26_out, nand_27_out);
  nand nand_32 (nand_32_out, nand_28_out, nand_29_out);
  T_Flip_Flop t_ff_1 (.clk(CLK), .T(nand_25_out), .Q(Q0));  // open: Qn, preset, reset, en
  T_Flip_Flop t_ff_2 (.clk(CLK), .T(nand_30_out), .Q(Q1));  // open: Qn, preset, reset, en
  T_Flip_Flop t_ff_3 (.clk(CLK), .T(nand_31_out), .Q(Q2));  // open: Qn, preset, reset, en
  T_Flip_Flop t_ff_4 (.clk(CLK), .T(nand_32_out), .Q(Q3));  // open: Qn, preset, reset, en
  Counter #(.width(6), .max('h24)) counter_1 (
    .Q({counter_1_q[5], Load, D3, counter_1_q[2:1], D0}), .carry(counter_1_carry), .clk(CLK));  // open: load, D, count, clr
  and and_5 (CLK, clock_1_out, not_1_out);
  not not_1 (not_1_out, counter_1_carry);
  Clock clock_1 (.out(clock_1_out));
  TTY #(.rows(1), .cols(37)) tty_1 (.data({2'b10, Carry, Q3, Q2, Q1, Q0}), .clk(CLK));  // open: we, clr
  not not_2 (Enable, counter_1_q[5]);
  or or_1 (D1, Enable, counter_1_q[1]);
  or or_2 (D2, counter_1_q[2], Load);

  // Notes on the sheet:
  //   @ABCDEFGHIJKLMN_@FGFGFGFGN_N_N_N0000
endmodule
