// Logisim project 6.circ as structural Verilog: 1 circuit, main circuit main
module main (
);

  wire _4_Counter_carry, A_q, A_qn, and_1_out, and_2_out, and_3_out, and_4_out, and_5_out, and_6_out,
       and_7_out, and_8_out, and_9_out, B_q, B_qn, C_q, C_qn, CLK, clock_1_out, go, not_1_out, or_1_out,
       or_2_out, or_3_out, Q, Reset_out, w;
  wire [1:0] _4_Counter_q;
  wire [4:0] _32_Counter_q;

  not not_1 (not_1_out, w);
  and and_1 (and_1_out, B_q, B_q, C_q);
  and and_2 (and_2_out, A_q, B_qn, C_qn);
  and and_3 (and_3_out, A_qn, B_q, w);
  and and_4 (and_4_out, A_q, B_q);
  and and_5 (and_5_out, A_qn, B_qn, C_q);
  and and_6 (and_6_out, A_qn, B_qn, not_1_out);
  and and_7 (and_7_out, A_q, B_q, C_q);
  and and_8 (and_8_out, A_qn, B_q, C_qn, not_1_out);
  and and_9 (and_9_out, A_qn, B_qn, C_qn, w);
  or or_1 (or_1_out, and_1_out, and_2_out, and_3_out);
  or or_2 (or_2_out, and_4_out, and_5_out, and_6_out);
  or or_3 (or_3_out, and_7_out, and_8_out, and_9_out);
  T_Flip_Flop A (.clk(CLK), .T(or_1_out), .Q(A_q), .Qn(A_qn));  // open: preset, reset, en
  T_Flip_Flop B (.clk(CLK), .T(or_2_out), .Q(B_q), .Qn(B_qn));  // open: preset, reset, en
  T_Flip_Flop C (.clk(CLK), .T(or_3_out), .Q(C_q), .Qn(C_qn));  // open: preset, reset, en
  TTY #(.rows(17), .cols(4)) tty_1 (.data({6'b011000, Q}), .clk(CLK), .we(go), .clr(Reset_out));
  and and_10 (Q, A_q, B_qn, w, C_qn);
  Button Reset (.out(Reset_out));
  // Probe on _4_Counter_q
  Counter #(.width(2), .max('h3)) _4_Counter (
    .Q(_4_Counter_q), .carry(_4_Counter_carry), .clk(CLK), .clr(Reset_out));  // open: load, D, count
  and and_11 (CLK, clock_1_out, go);
  Clock clock_1 (.out(clock_1_out));
  Counter #(.width(5), .max('h1f), .trigger("falling")) _32_Counter (
    .Q(_32_Counter_q), .clk(_4_Counter_carry), .clr(Reset_out));  // open: load, D, count, carry
  // Probe on _32_Counter_q[3:0]
  not not_2 (go, _32_Counter_q[4]);
  // Probe on w
  BitSelector #(.width(4)) bitselector_1 (.in(_32_Counter_q[3:0]), .out(w), .sel(_4_Counter_q));

  // Notes on the sheet:
  //   0000
  //   1000
  //   0100
  //   1100
  //   0010
  //   1010
  //   0110
  //   1110
  //   0001
  //   1001
  //   0101
  //   1101
  //   0011
  //   1011
  //   0111
  //   1111
  //   13 gates
  //   1
  //   1
endmodule
