// Logisim project 7.circ as structural Verilog: 1 circuit, main circuit main
module main (
);

  wire _5_Counter_carry, A_q, A_qn, and_1_out, and_2_out, and_3_out, and_4_out, and_5_out, and_6_out,
       and_7_out, and_8_out, and_9_out, and_10_out, and_11_out, and_12_out, and_13_out, and_14_out,
       and_15_out, and_16_out, and_17_out, and_18_out, B_q, B_qn, C_q, C_qn, CLK, clock_1_out, D_q, D_qn, go,
       not_1_out, or_1_out, or_2_out, or_3_out, or_4_out, p, Reset_out, w;
  wire [2:0] _5_Counter_q;
  wire [5:0] _64_Counter_q;

  not not_1 (not_1_out, w);
  and and_1 (and_1_out, A_qn, B_q, not_1_out);
  and and_2 (and_2_out, B_qn, D_q, w);
  and and_3 (and_3_out, A_qn, B_q, D_q);
  and and_4 (and_4_out, C_q, not_1_out);
  and and_5 (and_5_out, A_q, B_q, D_qn, w);
  and and_6 (and_6_out, B_qn, D_qn, not_1_out);
  and and_7 (and_7_out, A_qn, B_qn, D_q);
  and and_8 (and_8_out, B_q, D_q, not_1_out);
  and and_9 (and_9_out, B_q, C_q);
  and and_10 (and_10_out, A_q, B_q, C_qn, D_q, w);
  and and_11 (and_11_out, A_q, B_qn, not_1_out);
  and and_12 (and_12_out, B_qn, C_q);
  and and_13 (and_13_out, A_qn, B_q, D_q, not_1_out);
  and and_14 (and_14_out, A_qn, D_qn, w);
  and and_15 (and_15_out, B_qn, C_qn, w);
  and and_16 (and_16_out, A_q, D_qn, not_1_out);
  or or_1 (or_1_out, and_1_out, and_2_out, and_3_out, and_4_out);
  or or_2 (or_2_out, and_5_out, and_6_out, and_7_out, and_4_out, and_9_out, and_8_out);
  or or_3 (or_3_out, and_10_out, and_11_out, and_12_out, and_4_out);
  or or_4 (or_4_out, and_4_out, and_13_out, and_14_out, and_15_out, and_16_out);
  T_Flip_Flop A (.clk(CLK), .T(or_1_out), .Q(A_q), .Qn(A_qn));  // open: preset, reset, en
  T_Flip_Flop B (.clk(CLK), .T(or_2_out), .Q(B_q), .Qn(B_qn));  // open: preset, reset, en
  T_Flip_Flop C (.clk(CLK), .T(or_3_out), .Q(C_q), .Qn(C_qn));  // open: preset, reset, en
  T_Flip_Flop D (.clk(CLK), .T(or_4_out), .Q(D_q), .Qn(D_qn));  // open: preset, reset, en
  and and_17 (and_17_out, A_q, B_qn, C_qn, D_q, not_1_out);
  and and_18 (and_18_out, B_q, C_q, w);
  or or_5 (p, and_17_out, and_18_out);
  TTY #(.rows(33), .cols(5)) tty_1 (.data({6'b011000, p}), .clk(CLK), .we(go), .clr(Reset_out));
  // Probe on w
  Button Reset (.out(Reset_out));
  nand nand_1 (go, _64_Counter_q[0], _64_Counter_q[5]);
  and and_19 (CLK, clock_1_out, go);
  Clock clock_1 (.out(clock_1_out));
  // Probe on _5_Counter_q
  Counter #(.width(3), .max('h4)) _5_Counter (
    .Q(_5_Counter_q), .carry(_5_Counter_carry), .clk(CLK), .clr(Reset_out));  // open: load, D, count
  // Probe on _64_Counter_q
  BitSelector #(.width(6)) bitselector_1 (.in(_64_Counter_q), .out(w), .sel(_5_Counter_q));
  Counter #(.width(6), .max('h3f), .trigger("falling")) _64_Counter (
    .Q(_64_Counter_q), .clk(_5_Counter_carry), .clr(Reset_out));  // open: load, D, count, carry

  // Notes on the sheet:
  //   1  0
  //   1  3
  //   1  5
  //   1  6
  //   1  9
  //   1   10
  //   1  12
  //   1  15
  //   1  17
  //   1  18
  //   1  20
  //   1  23
  //   1  24
  //   1 27
  //   1  29
  //   1  30
  //   24 Gates
endmodule
