// Logisim project alu.circ as structural Verilog: 5 circuits, main circuit main
module main (
);

  wire A0, A1, A2, A3, A4, ADD, ADD_0, ADD_1, ADD_2, ADD_3, ADD_4, AND, AND_0, AND_1, AND_2, AND_3, AND_4,
       B0, B1, B2, B3, B4, C0, C1, C2, C3, C4, C5, CIN, clock_1_out, clock_2_out, go, HCLK, NOT, NOT_0,
       NOT_1, not_1_out, NOT_2, not_2_out, NOT_3, NOT_4, not_5_out, OR, OR_0, OR_1, OR_2, OR_3, OR_4, reset,
       S0, S1;
  wire [2:0] multiplexer_1_out;
  wire [6:1] counter_1_q;

  not u_not_1 (not_1_out, S1);
  not u_not_2 (not_2_out, S0);
  and u_AND (AND, not_2_out, not_1_out);
  and u_OR (OR, not_1_out, S0);
  and u_NOT_3 (NOT, S1, not_2_out);
  and u_ADD (ADD, S1, S0);
  or u_or_2 (C4, AND_4, OR_4, NOT_4, ADD_4);
  or u_or_3 (C3, AND_3, OR_3, NOT_3, ADD_3);
  or u_or_4 (C2, AND_2, OR_2, NOT_2, ADD_2);
  or or_5 (C1, AND_1, OR_1, NOT_1, ADD_1);
  or or_6 (C0, AND_0, OR_0, NOT_0, ADD_0);
  \or  or_7 (
    .OR_CODE(OR), .x4(A4), .x3(A3), .x2(A2), .x1(A1), .x0(A0), .y4(B4), .y3(B3), .y2(B2), .y1(B1), .y0(B0),
    .d0(OR_0), .d1(OR_1), .d2(OR_2), .d3(OR_3), .d4(OR_4));
  \and  u_and_2 (
    .AND_CODE(AND), .x4(A4), .x3(A3), .x2(A2), .x1(A1), .x0(A0), .y4(B4), .y3(B3), .y2(B2), .y1(B1), .y0(B0),
    .d0(AND_0), .d1(AND_1), .d2(AND_2), .d3(AND_3), .d4(AND_4));
  add u_add_2 (
    .ADD_CODE(ADD), .x4(A4), .x3(A3), .x2(A2), .x1(A1), .x0(A0), .carry_in(CIN), .y4(B4), .y3(B3), .y2(B2),
    .y1(B1), .y0(B0), .d0(ADD_0), .d1(ADD_1), .d2(ADD_2), .d3(ADD_3), .d4(ADD_4));  // open: d5
  add u_add_3 (
    .ADD_CODE(1'b1), .x4(A4), .x3(A3), .x2(A2), .x1(A1), .x0(A0), .carry_in(CIN), .y4(B4), .y3(B3), .y2(B2),
    .y1(B1), .y0(B0), .d5(C5));  // open: d0, d1, d2, d3, d4
  \not  u_not_4 (
    .NOT_CODE(NOT), .x4(A4), .x3(A3), .x2(A2), .x1(A1), .x0(A0), .d4(NOT_4), .d3(NOT_3), .d2(NOT_2),
    .d1(NOT_1), .d0(NOT_0));
  // Probe on {C5, C4, C3}
  // Probe on {C2, C1, C0}
  // Probe on multiplexer_1_out
  // Probe on {4'b0110, multiplexer_1_out}
  Multiplexer #(.width(3)) multiplexer_1 (
    .in0({C5, C4, C3}), .in1({C2, C1, C0}), .out(multiplexer_1_out), .sel(HCLK));  // open: en
  TTY #(.rows(32), .cols(2)) tty_1 (.data({4'b0110, multiplexer_1_out}), .clk(clock_1_out), .we(go), .clr(reset));
  Clock clock_1 (.out(clock_1_out));
  // Probe on {A4, A3, A2, A1, A0, CIN}
  // Probe on {B4, B3, B2, B1, B0}
  // Probe on S1
  Clock clock_2 (.out(clock_2_out));
  // Probe on S0
  not not_5 (not_5_out, HCLK);
  Counter #(.width(7), .max('h7f), .ongoal("stay")) counter_1 (
    .Q({counter_1_q, HCLK}), .clk(clock_2_out), .clr(reset));  // open: load, D, count, carry
  Button u_Reset (.out(reset));
  Random #(.width(13), .seed(34573)) random_1 (
    .clk(not_5_out), .next(go), .out({B4, B3, B2, B1, B0, A4, A3, A2, A1, A0, CIN, S1, S0}), .clr(reset));
  not not_6 (go, counter_1_q[6]);

  // Notes on the sheet:
  //   07
  //   51
  //   40
  //   51
  //   77
  //   77
  //   57
  //   63
  //   43
  //   77
  //   60
  //   51
  //   46
  //   71
  //   32
  //   43
  //   34
  //   50
  //   53
  //   00
  //   07
  //   02
  //   74
  //   04
  //   35
  //   52
  //   52
  //   50
  //   65
  //   46
  //   11
  //   57
endmodule

module \not  (
  input  x4,
  input  x3,
  input  x2,
  input  x1,
  input  x0,
  input  NOT_CODE,
  output d4,
  output d3,
  output d2,
  output d1,
  output d0
);

  wire not_1_out, not_2_out, not_3_out, not_4_out, not_5_out;

  not not_1 (not_1_out, x4);
  and and_1 (d4, NOT_CODE, not_1_out);
  not not_2 (not_2_out, x2);
  not not_3 (not_3_out, x3);
  and and_2 (d3, NOT_CODE, not_3_out);
  and and_3 (d2, NOT_CODE, not_2_out);
  not not_4 (not_4_out, x1);
  and and_4 (d1, NOT_CODE, not_4_out);
  not not_5 (not_5_out, x0);
  and and_5 (d0, NOT_CODE, not_5_out);
endmodule

module \or  (
  input  x4,
  input  x3,
  input  x2,
  input  x1,
  input  x0,
  input  OR_CODE,
  input  y4,
  input  y3,
  input  y2,
  input  y1,
  input  y0,
  output d0,
  output d1,
  output d2,
  output d3,
  output d4
);

  wire or_1_out, or_2_out, or_3_out, or_4_out, or_5_out;

  or or_1 (or_1_out, x0, y0);
  or or_2 (or_2_out, x1, y1);
  or or_3 (or_3_out, x2, y2);
  or or_4 (or_4_out, x3, y3);
  or or_5 (or_5_out, y4, x4);
  and and_1 (d0, OR_CODE, or_1_out);
  and and_2 (d1, OR_CODE, or_2_out);
  and and_3 (d2, OR_CODE, or_3_out);
  and and_4 (d3, OR_CODE, or_4_out);
  and and_5 (d4, OR_CODE, or_5_out);
endmodule

module \and  (
  input  x4,
  input  x3,
  input  x2,
  input  x1,
  input  x0,
  input  AND_CODE,
  input  y4,
  input  y3,
  input  y2,
  input  y1,
  input  y0,
  output d0,
  output d1,
  output d2,
  output d3,
  output d4
);

  and and_1 (d0, x0, AND_CODE, y0);
  and and_2 (d1, x1, AND_CODE, y1);
  and and_3 (d2, AND_CODE, x2, y2);
  and and_4 (d3, x3, AND_CODE, y3);
  and and_5 (d4, AND_CODE, y4, x4);
endmodule

module add (
  input  y4,
  input  y3,
  input  y2,
  input  y1,
  input  y0,
  input  x4,
  input  x3,
  input  x2,
  input  x1,
  input  x0,
  input  carry_in,
  input  ADD_CODE,
  output d0,
  output d1,
  output d2,
  output d5,
  output d3,
  output d4
);

  wire and_11_out, and_12_out, and_13_out, and_14_out, and_15_out, and_16_out, and_17_out, and_18_out,
       and_19_out, and_20_out, and_21_out, and_22_out, and_23_out, and_24_out, and_25_out, G0, G1, G2, G3,
       G4, K1, K2, K3, K4, or_10_out, P0, P1, P2, P3, P4, xor_1_out, xor_2_out, xor_3_out, xor_4_out,
       xor_5_out, xor_6_out, xor_7_out, xor_8_out, xor_9_out, xor_10_out;

  xor xor_1 (xor_1_out, x0, y0);
  xor xor_2 (xor_2_out, y1, x1);
  xor xor_3 (xor_3_out, y2, x2);
  xor xor_4 (xor_4_out, y3, x3);
  xor xor_5 (xor_5_out, y4, x4);
  and and_1 (G0, x0, y0);
  or or_1 (P0, x0, y0);
  and and_2 (G1, x1, y1);
  or or_2 (P1, x1, y1);
  and and_3 (G2, x2, y2);
  or or_3 (P2, x2, y2);
  and and_4 (G3, x3, y3);
  or or_4 (P3, x3, y3);
  and and_5 (G4, x4, y4);
  or or_5 (P4, x4, y4);
  xor xor_6 (xor_6_out, xor_1_out, carry_in);
  xor xor_7 (xor_7_out, xor_2_out, K1);
  xor xor_8 (xor_8_out, xor_3_out, K2);
  xor xor_9 (xor_9_out, xor_4_out, K3);
  xor xor_10 (xor_10_out, xor_5_out, K4);
  and and_6 (d0, ADD_CODE, xor_6_out);
  and and_7 (d1, ADD_CODE, xor_7_out);
  and and_8 (d2, ADD_CODE, xor_8_out);
  and and_9 (d3, ADD_CODE, xor_9_out);
  and and_10 (d4, ADD_CODE, xor_10_out);
  and and_11 (and_11_out, carry_in, P0);
  and and_12 (and_12_out, P0, P1, carry_in);
  and and_13 (and_13_out, P1, G0);
  and and_14 (and_14_out, P0, P1, P2, carry_in);
  and and_15 (and_15_out, G0, P1, P2);
  and and_16 (and_16_out, G1, P2);
  and and_17 (and_17_out, carry_in, P0, P1, P2, P3);
  and and_18 (and_18_out, P1, P2, P3, G0);
  and and_19 (and_19_out, P2, P3, G1);
  and and_20 (and_20_out, P3, G2);
  and and_21 (and_21_out, carry_in, P0, P1, P2, P3, P4);
  and and_22 (and_22_out, G0, P0, P1, P2, P3, P4);
  and and_23 (and_23_out, G1, P2, P3, P4);
  and and_24 (and_24_out, G2, P3, P4);
  and and_25 (and_25_out, G3, P4);
  or or_6 (K1, and_11_out, G0);
  or or_7 (K2, and_12_out, G1, and_13_out);
  or or_8 (K3, and_14_out, G2, and_15_out, and_16_out);
  or or_9 (K4, and_17_out, and_18_out, G3, and_19_out, and_20_out);
  or or_10 (or_10_out, and_21_out, and_22_out, G4, and_23_out, and_24_out, and_25_out);
  and and_26 (d5, ADD_CODE, or_10_out);

  // Other names for the same wires on the sheet: K0 = carry_in
endmodule
