// Logisim project cpu.circ as structural Verilog: 9 circuits, main circuit main
module main (
  output [9:0] out_1,
  output [9:0] out_2,
  output [9:0] out_3,
  output [9:0] out_4,
  output [9:0] out_5,
  output [9:0] out_6,
  output [9:0] out_7,
  output ignore,
  output halt
);

  wire and_1_out, and_2_out, CLK, clock_1_out, comparator_1_lt, comparator_2_lt, DEC_Enable, HALT_t,
       not_1_out, not_2_out, not_3_out, not_4_out, NZ, PCSel, t_ff_2_q, TClock;
  wire [1:0] counter_2_q, Upper_2_bits;
  wire [2:0] B, dest, rom_1_data;
  wire [3:0] B_SEL, control_1_aluctrl;
  wire [4:0] alu2_1_c, counter_1_q, multiplexer_1_out, pcount_1_c;
  wire [6:0] adder_1_out, adder_2_out, ASCII, decoder_1_out0, LSB, MiddleBits;
  wire [7:0] multiplexer_5_out;
  wire [9:0] alu_1_c, DATA, multiplexer_2_out, multiplexer_3_out, multiplexer_4_out;
  wire [23:13] ram_1_data;

  // Probe on pcount_1_c
  ALU2 alu2_1 (.A(multiplexer_1_out), .B(pcount_1_c), .C(alu2_1_c), .SEL(4'b0011));
  PCount pcount_1 (.CIN(alu2_1_c), .CLOCK(not_1_out), .EN(not_2_out), .C(pcount_1_c));
  not not_1 (not_1_out, CLK);
  // Probe on multiplexer_1_out
  Multiplexer #(.width(5)) multiplexer_1 (
    .in0(5'b00001), .in1(DATA[4:0]), .out(multiplexer_1_out), .sel(and_1_out));  // open: en
  // Probe on alu2_1_c
  not not_2 (not_2_out, HALT_t);
  RAM #(.addrWidth(5), .dataWidth(24)) ram_1 (
    .addr(pcount_1_c), .data({ram_1_data[23:19], dest, ram_1_data[15:13], B, DATA}), .clk(CLK));  // open: sel, ld, clr
  and and_1 (and_1_out, PCSel, NZ);
  // Probe on ram_1_data[23:19]
  // Probe on DATA[4:0]
  // Probe on DATA
  // Probe on ram_1_data[15:13]
  Control control_1 (
    .CIN(ram_1_data[23:19]), .B(B), .DEST(dest), .CLOCK(CLK), .ALUCTRL(control_1_aluctrl), .BSELECT(B_SEL),
    .BNEZ(PCSel), .DEC_EN(DEC_Enable), .HALT(HALT_t));
  Decoder #(.select(3), .disabled(0)) decoder_1 (
    .out0(decoder_1_out0[0]), .out1(decoder_1_out0[1]), .out2(decoder_1_out0[2]), .out3(decoder_1_out0[3]),
    .out4(decoder_1_out0[4]), .out5(decoder_1_out0[5]), .out6(decoder_1_out0[6]), .sel(dest), .en(not_3_out));  // open: out7
  not not_3 (not_3_out, DEC_Enable);
  // Probe on dest
  Multiplexer #(.select(3), .width(10), .disabled(0)) multiplexer_2 (
    .in0(out_1), .in1(out_2), .in2(out_3), .in3(out_4), .in4(out_5), .in5(out_6), .in6(out_7),
    .out(multiplexer_2_out), .sel(ram_1_data[15:13]));  // open: in7, en
  // Probe on multiplexer_2_out
  // Probe on control_1_aluctrl
  // Probe on B_SEL
  ALU alu_1 (.B(multiplexer_3_out), .A(multiplexer_2_out), .Selector(control_1_aluctrl), .C(alu_1_c));
  // Probe on {ram_1_data[23:19], dest, ram_1_data[15:13], B, DATA}
  // Probe on decoder_1_out0
  Multiplexer #(.select(4), .width(10), .disabled(0)) multiplexer_3 (
    .in0(out_1), .in1(out_2), .in2(out_3), .in3(out_4), .in4(out_5), .in5(out_6), .in6(out_7),
    .in7({10{1'b0}}), .in8(DATA), .out(multiplexer_3_out), .sel(B_SEL));  // open: in9, in10, in11, in12, in13, in14, in15, en
  // Probe on multiplexer_3_out
  // Probe on alu_1_c
  regbank regbank_1 (
    .EN(decoder_1_out0), .CLK(CLK), .IN(alu_1_c), .R0(out_1), .R1(out_2), .R2(out_3), .R3(out_4), .R4(out_5),
    .R5(out_6), .R6(out_7));
  Multiplexer #(.select(3), .width(10), .disabled(0)) multiplexer_4 (
    .in0(out_1), .in1(out_2), .in2(out_3), .in3(out_4), .in4(out_5), .in5(out_6), .in6(out_7),
    .out(multiplexer_4_out), .sel(dest));  // open: in7, en
  TTY #(.rows(33), .cols(4)) tty_1 (.data(ASCII), .clk(TClock));  // open: we, clr
  // Probe on out_1
  // Probe on out_5
  Counter #(.width(5), .max('h1f), .ongoal("stay")) counter_1 (
    .Q(counter_1_q), .carry(halt), .clk(CLK));  // open: load, D, count, clr
  // Probe on out_2
  // Probe on out_6
  Multiplexer #(.select(3), .width(10)) multiplexer_5 (
    .in0(out_1), .in1(out_2), .in2(out_3), .in3(out_4), .in4(out_5), .in5(out_6), .in6(out_7),
    .out({Upper_2_bits, multiplexer_5_out}), .sel(rom_1_data));  // open: in7, en
  not not_4 (not_4_out, halt);
  Clock clock_1 (.out(clock_1_out));
  or or_1 (NZ, multiplexer_4_out[0], multiplexer_4_out[1], multiplexer_4_out[2], multiplexer_4_out[3], multiplexer_4_out[4], multiplexer_4_out[5], multiplexer_4_out[6], multiplexer_4_out[7], multiplexer_4_out[8], multiplexer_4_out[9]);
  ROM #(.addrWidth(5), .dataWidth(3)) rom_1 (.addr(counter_1_q), .data(rom_1_data));  // open: sel
  and and_2 (and_2_out, not_4_out, clock_1_out);
  not not_5 (TClock, and_2_out);
  // Probe on out_3
  // Probe on out_7
  // Probe on out_4
  Comparator #(.width(7)) comparator_1 (
    .a(7'b0111001), .b({3'b011, multiplexer_5_out[3:0]}), .lt(comparator_1_lt));  // open: gt, eq
  Comparator #(.width(7)) comparator_2 (
    .a(7'b0111001), .b({3'b011, multiplexer_5_out[7:4]}), .lt(comparator_2_lt));  // open: gt, eq
  T_Flip_Flop t_ff_1 (.clk(t_ff_2_q), .T(1'b1), .Q(CLK));  // open: Qn, preset, reset, en
  T_Flip_Flop t_ff_2 (.clk(and_2_out), .T(1'b1), .Q(t_ff_2_q));  // open: Qn, preset, reset, en
  Adder #(.width(7)) adder_1 (
    .a({3'b011, multiplexer_5_out[3:0]}), .b(7'b0000111), .out(adder_1_out));  // open: cin, cout
  Adder #(.width(7)) adder_2 (
    .a({3'b011, multiplexer_5_out[7:4]}), .b(7'b0000111), .out(adder_2_out));  // open: cin, cout
  Multiplexer #(.select(2), .width(7)) multiplexer_6 (
    .in0({5'b01100, Upper_2_bits}), .in1(MiddleBits), .in2(LSB), .in3(7'b0100000), .out(ASCII),
    .sel(counter_2_q));  // open: en
  Counter #(.width(2), .max('h3)) counter_2 (.Q(counter_2_q), .clk(TClock));  // open: load, D, count, carry, clr
  Multiplexer #(.width(7), .disabled(0), .enable("false")) multiplexer_7 (
    .in0({3'b011, multiplexer_5_out[3:0]}), .in1(adder_1_out), .out(LSB), .sel(comparator_1_lt));
  Multiplexer #(.width(7), .disabled(0), .enable("false")) multiplexer_8 (
    .in0({3'b011, multiplexer_5_out[7:4]}), .in1(adder_2_out), .out(MiddleBits), .sel(comparator_2_lt));
  T_Flip_Flop t_ff_3 (.clk(CLK), .T(1'b1), .Q(ignore));  // open: Qn, preset, reset, en

  // Other names for the same wires on the sheet: R0[9:0] = out_1; R1[9:0] = out_2; R2[9:0] = out_3; R3[9:0] = out_4;
  //   R4[9:0] = out_5; R5[9:0] = out_6; R6[9:0] = out_7

  // Notes on the sheet:
  //   DO NOT PUT ANY PINS ON THE main circuit.  (You should not need any anyway.)
  //   0F5
  //   0F5
  //   25A
  //   050
  //   2FF
  //   30A
  //   34F
  //   0F5
  //   1EA
  //   07A
  //   29B
  //   165
  //   10F
  //   0F5
  //   0AA
  //   0AA
  //   05A
  //   00A
  //   0FA
  //   104
  //   0B4
  //   165
  //   165
  //   001
  //   001
  //   000
  //   000
  //   000
  //   000
  //   000
  //   ???
  //   There is no Reset.  Just Ctrl-r, then load test.txt into your RAM, and then Ctrl-k
  //   You must  use the CLK tunnel for the source of your clock.  R0-R6 are the other tunnels you need to connect
  //   contents of rom_1 (hex, n*v repeats v):
  //   0 0 0 1 2 3 4 5 6 2 3 4 5 6 0 0 0 1 3 4 6 3 5 5 8*6
endmodule

module register (
  input  CLK,
  input  EN,
  input  [9:0] IN,
  output [9:0] OUT
);

  D_Flip_Flop d_ff_1 (.clk(CLK), .D(IN[0]), .Q(OUT[0]), .en(EN));  // open: Qn, preset, reset
  D_Flip_Flop d_ff_2 (.clk(CLK), .D(IN[1]), .Q(OUT[1]), .en(EN));  // open: Qn, preset, reset
  D_Flip_Flop d_ff_3 (.clk(CLK), .D(IN[2]), .Q(OUT[2]), .en(EN));  // open: Qn, preset, reset
  D_Flip_Flop d_ff_4 (.clk(CLK), .D(IN[3]), .Q(OUT[3]), .en(EN));  // open: Qn, preset, reset
  D_Flip_Flop d_ff_5 (.clk(CLK), .D(IN[4]), .Q(OUT[4]), .en(EN));  // open: Qn, preset, reset
  D_Flip_Flop d_ff_6 (.clk(CLK), .D(IN[5]), .Q(OUT[5]), .en(EN));  // open: Qn, preset, reset
  D_Flip_Flop d_ff_7 (.clk(CLK), .D(IN[6]), .Q(OUT[6]), .en(EN));  // open: Qn, preset, reset
  D_Flip_Flop d_ff_8 (.clk(CLK), .D(IN[7]), .Q(OUT[7]), .en(EN));  // open: Qn, preset, reset
  D_Flip_Flop d_ff_9 (.clk(CLK), .D(IN[8]), .Q(OUT[8]), .en(EN));  // open: Qn, preset, reset
  D_Flip_Flop d_ff_10 (.clk(CLK), .D(IN[9]), .Q(OUT[9]), .en(EN));  // open: Qn, preset, reset
endmodule

module regbank (
  input  [6:0] EN,
  input  CLK,
  input  [9:0] IN,
  output [9:0] R0,
  output [9:0] R1,
  output [9:0] R2,
  output [9:0] R3,
  output [9:0] R4,
  output [9:0] R5,
  output [9:0] R6
);

  register register_1 (.IN(IN), .CLK(CLK), .EN(EN[5]), .OUT(R5));
  register register_2 (.IN(IN), .CLK(CLK), .EN(EN[6]), .OUT(R6));
  register register_3 (.IN(IN), .CLK(CLK), .EN(EN[4]), .OUT(R4));
  register register_4 (.IN(IN), .CLK(CLK), .EN(EN[3]), .OUT(R3));
  register register_5 (.IN(IN), .CLK(CLK), .EN(EN[2]), .OUT(R2));
  register register_6 (.IN(IN), .CLK(CLK), .EN(EN[1]), .OUT(R1));
  register register_7 (.IN(IN), .CLK(CLK), .EN(EN[0]), .OUT(R0));
endmodule

module ALU (
  input  [3:0] Selector,
  input  [9:0] A,
  input  [9:0] B,
  output [9:0] C
);

  wire B0, B1, B2, B3, B4, B5, B6, B7, B8, B9, C10, CIN, CIN1, CIN2, CIN3, CIN4, CIN5, CIN6, CIN7, CIN8,
       CIN9, G0, G1, G2, G3, G4, G5, G6, G7, G8, G9, P0, P1, P2, P3, P4, P5, P6, P7, P8, P9;
  wire [9:0] not_1_out;

  BitALU bitalu_1 (.A(A[0]), .B(B0), .CIN(CIN), .SLL(1'b0), .SRL(A[1]), .P(P0), .G(G0), .C(C[0]), .SEL(Selector));
  BitALU bitalu_2 (.A(A[1]), .B(B1), .CIN(CIN1), .SLL(A[0]), .SRL(A[2]), .P(P1), .G(G1), .C(C[1]), .SEL(Selector));
  BitALU bitalu_3 (.A(A[2]), .B(B2), .CIN(CIN2), .SLL(A[1]), .SRL(A[3]), .P(P2), .G(G2), .C(C[2]), .SEL(Selector));
  BitALU bitalu_4 (.A(A[3]), .B(B3), .CIN(CIN3), .SLL(A[2]), .SRL(A[4]), .P(P3), .G(G3), .C(C[3]), .SEL(Selector));
  BitALU bitalu_5 (.A(A[4]), .B(B4), .CIN(CIN4), .SLL(A[3]), .SRL(A[5]), .P(P4), .G(G4), .C(C[4]), .SEL(Selector));
  BitALU bitalu_6 (.A(A[5]), .B(B5), .CIN(CIN5), .SLL(A[4]), .SRL(A[6]), .P(P5), .G(G5), .C(C[5]), .SEL(Selector));
  BitALU bitalu_7 (.A(A[6]), .B(B6), .CIN(CIN6), .SLL(A[5]), .SRL(A[7]), .P(P6), .G(G6), .C(C[6]), .SEL(Selector));
  BitALU bitalu_8 (.A(A[7]), .B(B7), .CIN(CIN7), .SLL(A[6]), .SRL(A[8]), .P(P7), .G(G7), .C(C[7]), .SEL(Selector));
  BitALU bitalu_9 (.A(A[8]), .B(B8), .CIN(CIN8), .SLL(A[7]), .SRL(A[9]), .P(P8), .G(G8), .C(C[8]), .SEL(Selector));
  BitALU bitalu_10 (.A(A[9]), .B(B9), .CIN(CIN9), .SLL(A[8]), .SRL(1'b0), .P(P9), .G(G9), .C(C[9]), .SEL(Selector));
  Multiplexer #(.select(4)) multiplexer_1 (
    .in0(1'b0), .in1(1'b0), .in2(1'b0), .in3(1'b0), .in4(1'b0), .in5(1'b0), .in6(1'b0), .in7(1'b1),
    .in8(1'b0), .in9(1'b0), .in10(1'b0), .in11(1'b0), .in12(1'b0), .in13(1'b0), .in14(1'b0), .in15(1'b0),
    .out(CIN), .sel(Selector));  // open: en
  CLA cla_1 (
    .CIN(CIN), .G0(G0), .P0(P0), .G1(G1), .P1(P1), .G2(G2), .P2(P2), .G3(G3), .P3(P3), .G4(G4), .P4(P4),
    .Cout0(CIN1), .Cout1(CIN2), .Cout2(CIN3), .Cout3(CIN4), .Cout4(CIN5));
  assign not_1_out = ~B;  // NOT_Gate not_1, 10 bits wide
  Multiplexer #(.select(4), .width(10)) multiplexer_2 (
    .in0(B), .in1(B), .in2(B), .in3(B), .in4(B), .in5(B), .in6(B), .in7(not_1_out), .in8(B),
    .out({B9, B8, B7, B6, B5, B4, B3, B2, B1, B0}), .sel(Selector));  // open: in9, in10, in11, in12, in13, in14, in15, en
  CLA cla_2 (
    .CIN(CIN5), .G0(G5), .P0(P5), .G1(G6), .P1(P6), .G2(G7), .P2(P7), .G3(G8), .P3(P8), .G4(G9), .P4(P9),
    .Cout0(CIN6), .Cout1(CIN7), .Cout2(CIN8), .Cout3(CIN9), .Cout4(C10));

  // Other names for the same wires on the sheet: SEL[3:0] = Selector
endmodule

module PCount (
  input  CLOCK,
  input  EN,
  input  [4:0] CIN,
  output [4:0] C
);

  D_Flip_Flop d_ff_1 (.clk(CLOCK), .D(CIN[0]), .Q(C[0]), .en(EN));  // open: Qn, preset, reset
  D_Flip_Flop d_ff_2 (.clk(CLOCK), .D(CIN[1]), .Q(C[1]), .en(EN));  // open: Qn, preset, reset
  D_Flip_Flop d_ff_3 (.clk(CLOCK), .D(CIN[2]), .Q(C[2]), .en(EN));  // open: Qn, preset, reset
  D_Flip_Flop d_ff_4 (.clk(CLOCK), .D(CIN[3]), .Q(C[3]), .en(EN));  // open: Qn, preset, reset
  D_Flip_Flop d_ff_5 (.clk(CLOCK), .D(CIN[4]), .Q(C[4]), .en(EN));  // open: Qn, preset, reset
endmodule

module Control (
  input  [4:0] CIN,
  input  [2:0] B,
  input  [2:0] DEST,
  input  CLOCK,
  output [3:0] ALUCTRL,
  output [3:0] BSELECT,
  output BNEZ,
  output DEC_EN,
  output HALT
);

  wire decoder_1_out12, decoder_1_out15;

  Multiplexer #(.select(4), .width(4)) multiplexer_1 (
    .in0(4'b0000), .in1(4'b0001), .in2(4'b0010), .in3(4'b0011), .in4(4'b0100), .in5(4'b0101), .in6(4'b0110),
    .in7(4'b0111), .in8(4'b0011), .in9(4'b0111), .in10(4'b1000), .out(ALUCTRL), .sel(CIN[3:0]));  // open: in11, in12, in13, in14, in15, en
  Multiplexer #(.select(4), .width(4)) multiplexer_2 (
    .in0({1'b0, B}), .in1({1'b0, B}), .in2({1'b0, DEST}), .in3({1'b0, B}), .in4({1'b0, DEST}),
    .in5({1'b0, DEST}), .in6({1'b0, DEST}), .in7({1'b0, B}), .in8(4'b1000), .in9(4'b1000), .in10(4'b1000),
    .in11(4'b1000), .in12(4'b1000), .in13(4'b1000), .in14(4'b1000), .in15(4'b1000), .out(BSELECT),
    .sel(CIN[3:0]));  // open: en
  Decoder #(.select(4)) decoder_1 (
    .out11(BNEZ), .out12(decoder_1_out12), .out15(decoder_1_out15), .sel(CIN[3:0]));  // open: out0, out1, out2, out3, out4, out5, out6, out7, out8, out9, out10, out13, out14, en
  buf and_1 (HALT, decoder_1_out15);  // AND_Gate
  or or_1 (DEC_EN, BNEZ, decoder_1_out12, decoder_1_out15);
endmodule

module BitALU (
  input  A,
  input  B,
  input  CIN,
  input  SLL,
  input  SRL,
  input  [3:0] SEL,
  output P,
  output G,
  output C
);

  wire not_1_out, xor_1_out, xor_2_out;

  and and_1 (G, A, B);
  or or_1 (P, A, B);
  not not_1 (not_1_out, A);
  xor xor_1 (xor_1_out, B, A);
  xor xor_2 (xor_2_out, xor_1_out, CIN);
  Multiplexer #(.select(4)) multiplexer_1 (
    .in0(G), .in1(P), .in2(not_1_out), .in3(xor_2_out), .in4(A), .in5(SLL), .in6(SRL), .in7(xor_2_out),
    .in8(B), .out(C), .sel(SEL));  // open: in9, in10, in11, in12, in13, in14, in15, en
endmodule

module CLA (
  input  CIN,
  input  G0,
  input  P0,
  input  G1,
  input  P1,
  input  G2,
  input  P2,
  input  G3,
  input  P3,
  input  G4,
  input  P4,
  output Cout0,
  output Cout1,
  output Cout2,
  output Cout3,
  output Cout4
);

  wire P0CIN_out, P01CIN_out, P1G0_out, P2G1_out, P3G2_out, P4G3_out, P012CIN_out, P12G0_out, P23G1_out,
       P34G2_out, P0123CIN_out, P123G0_out, P234G1_out, P01234CIN_out, P1234G0_out;

  and P0CIN (P0CIN_out, P0, CIN);
  and P1G0 (P1G0_out, P1, G0);
  and P01CIN (P01CIN_out, P0, P1, CIN);
  and P2G1 (P2G1_out, P2, G1);
  and P12G0 (P12G0_out, P1, P2, G0);
  and P012CIN (P012CIN_out, P0, P1, P2, CIN);
  and P3G2 (P3G2_out, P3, G2);
  and P23G1 (P23G1_out, P2, P3, G1);
  and P123G0 (P123G0_out, P1, P2, P3, G0);
  and P0123CIN (P0123CIN_out, P0, P1, P2, P3, CIN);
  and P4G3 (P4G3_out, P4, G3);
  and P34G2 (P34G2_out, P3, P4, G2);
  and P234G1 (P234G1_out, P2, P3, P4, G1);
  and P1234G0 (P1234G0_out, P1, P2, P3, P4, G0);
  and P01234CIN (P01234CIN_out, P0, P1, P2, P3, P4, CIN);
  or or_1 (Cout0, P0CIN_out, G0);
  or or_2 (Cout1, P1G0_out, P01CIN_out, G1);
  or or_3 (Cout2, P2G1_out, P12G0_out, P012CIN_out, G2);
  or or_4 (Cout3, P3G2_out, P23G1_out, P123G0_out, P0123CIN_out, G3);
  or or_5 (Cout4, P4G3_out, P34G2_out, P234G1_out, P1234G0_out, P01234CIN_out, G4);
endmodule

module ALU2 (
  input  [4:0] A,
  input  [4:0] B,
  input  [3:0] SEL,
  output [4:0] C
);

  wire CIN1, CIN2, CIN3, CIN4, CIN5, G0, G1, G2, G3, G4, P0, P1, P2, P3, P4;

  BitALU bitalu_1 (.A(A[0]), .B(B[0]), .CIN(1'b0), .SLL(1'b0), .SRL(A[1]), .P(P0), .G(G0), .C(C[0]), .SEL(SEL));
  BitALU bitalu_2 (.A(A[1]), .B(B[1]), .CIN(CIN1), .SLL(A[0]), .SRL(A[2]), .P(P1), .G(G1), .C(C[1]), .SEL(SEL));
  BitALU bitalu_3 (.A(A[2]), .B(B[2]), .CIN(CIN2), .SLL(A[1]), .SRL(A[3]), .P(P2), .G(G2), .C(C[2]), .SEL(SEL));
  BitALU bitalu_4 (.A(A[3]), .B(B[3]), .CIN(CIN3), .SLL(A[2]), .SRL(A[4]), .P(P3), .G(G3), .C(C[3]), .SEL(SEL));
  BitALU bitalu_5 (.A(A[4]), .B(B[4]), .CIN(CIN4), .SLL(A[3]), .SRL(1'b0), .P(P4), .G(G4), .C(C[4]), .SEL(SEL));
  // Probe on SEL
  CLA cla_1 (
    .CIN(1'b0), .G0(G0), .P0(P0), .G1(G1), .P1(P1), .G2(G2), .P2(P2), .G3(G3), .P3(P3), .G4(G4), .P4(P4),
    .Cout0(CIN1), .Cout1(CIN2), .Cout2(CIN3), .Cout3(CIN4), .Cout4(CIN5));
endmodule
